# Fritzing sketch esp8266_lamp_sheme (saved by Fritzing 0.9.3b)
circuit board: 6cm x 4cm

parts:
  Часть1 = Adafruit ADS1115 16Bit I2C ADC [part_number="Adafruit #1085"]
  WeMos_D1_Mini1 = WeMos D1 Mini
  Часть2 = Adafruit MAX9814 Electret Microphone Amplifier [part_number="Adafruit #1713"]
  Encoder_round1 = Encoder round
  U1 = WS2812 RGB LED strip
  D1 = Rectifier Diode [part_number=1N4001 package="300 mil [THT]"]
  J1 = COMPUTER-PERIPHERAL-POWER [package=computer-peripheral-power-ra]
  LED1 = LED - 5mm [color="Red (633nm)" package="5 mm [THT]"]
  VR1 = Trimpot-#3296-flat [package=3386u]
  J2 = COMPUTER-PERIPHERAL-POWER [package=computer-peripheral-power-ra]
  R3 = Photocell (LDR) [package=THT]
  JP1 = Header 1 [package=1x01_offset]
  JP3 = Header 1 [package=1x01_offset]
  R5 = Resistor [tolerance=±5% resistance=100 package=THT]
  R7 = Resistor [tolerance=±5% resistance=100 package=THT]
  R8 = Resistor [tolerance=±5% resistance=10k package=THT]
  C1 = Electrolytic Capacitor [capacitance=1mF package="100 mil [THT, electrolytic]"]
  Q1 = Basic FET N-Channel [package="DPak [SMD]"]
  Pad2 = Pad [width=4 height=2 connect=center]
  Pad3 = Pad [width=4 height=2 connect=center]
  Pad4 = Pad [width=4 height=2 connect=center]
  Pad5 = Pad [width=4 height=2 connect=center]
  Pad6 = Pad [width=4 height=2 connect=center]
  Pad7 = Pad [width=4 height=2 connect=center]
  Pad8 = Pad [width=4 height=2 connect=center]  # not connected
  Pad9 = Pad [width=4 height=2 connect=center]
  Pad10 = Pad [width=4 height=2 connect=center]
  Pad11 = Pad [width=4 height=2 connect=center]
  Pad12 = Pad [width=4 height=2 connect=center]
  Pad14 = Pad [width=4 height=2 connect=center]
  Pad15 = Pad [width=4 height=2 connect=center]
  Pad16 = Pad [width=4 height=2 connect=center]  # not connected
  Pad17 = Pad [width=4 height=2 connect=center]  # not connected
  Pad18 = Pad [width=4 height=2 connect=center]  # not connected
  Pad19 = Pad [width=4 height=2 connect=center]  # not connected
  Pad20 = Pad [width=4 height=2 connect=center]  # not connected
  Pad21 = Pad [width=4 height=2 connect=center]  # not connected
  Pad22 = Pad [width=4 height=2 connect=center]  # not connected
  Pad23 = Pad [width=4 height=2 connect=center]  # not connected
  Pad24 = Pad [width=4 height=2 connect=center]  # not connected
  Pad25 = Pad [width=4 height=2 connect=center]  # not connected
  Pad26 = Pad [width=4 height=2 connect=center]  # not connected
  Pad27 = Pad [width=4 height=2 connect=center]  # not connected
  Pad28 = Pad [width=4 height=2 connect=center]  # not connected
  R4 = Resistor [tolerance=±5% resistance=100 package=THT]

nets:
  N1: Часть1.AIN0, VR1.CW, R3.pin_0
  N2: Часть1.SDA, WeMos_D1_Mini1.D1
  N3: Часть1.SCL, WeMos_D1_Mini1.D2
  GND: Часть1.GND, WeMos_D1_Mini1.G, Часть2.GND, Encoder_round1.pin1, D1.anode, LED1.cathode, VR1.WIPER
  VDD: Часть1.VDD, WeMos_D1_Mini1.3V3, Часть2.VDD, Encoder_round1.pin5, R3.pin_1
  5V: WeMos_D1_Mini1.5V, U1.VCC, J1.5V, J2.5V, JP1.1, C1.+, Pad2.pad, Pad3.pad, Pad4.pad, Pad5.pad
  N4: WeMos_D1_Mini1.A0, Часть2.OUTPUT
  N5: WeMos_D1_Mini1.D0, Encoder_round1.pin3, Pad12.pad
  N6: WeMos_D1_Mini1.D4, R4.Pin_1
  N7: WeMos_D1_Mini1.D5, Encoder_round1.pin2, Pad15.pad
  N8: WeMos_D1_Mini1.D6, R5.Pin_1
  N9: WeMos_D1_Mini1.D7, Encoder_round1.pin4, Pad14.pad
  N10: WeMos_D1_Mini1.D8, R7.Pin_1
  N11: U1.GND, Q1.drain
  N12: U1.DIN, R5.Pin_0, Pad11.pad
  GND_2: D1.cathode, J1.GND, J2.GND, JP3.1, R8.Pin_1, C1.-, Q1.source, Pad6.pad, Pad9.pad
  N13: LED1.anode, R4.Pin_0
  N14: R7.Pin_0, R8.Pin_0, Q1.Gate
  N15: Pad7.pad, Pad10.pad

custom parts:
  Adafruit ADS1115 16Bit I2C ADC: For microcontrollers without an analog-to-digital converter or when you want a higher-precision ADC, the ADS1115 provides 16-bit precision at 860 samples/second over I2C. The chip can be configured as 4 single-ended input channels, or two differential channels. As a nice bonus, it even includes a programmable gain amplifier, up to x16, to help boost up smaller single/differential signals to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
  Adafruit MAX9814 Electret Microphone Amplifier: Add an ear to your project with this well-designed electret microphone amplifier with AGC. This fully assembled and tested board comes with a 20-20KHz electret microphone soldered on. For the amplification, we use the Maxim MAX9814, a specialty chip that is designed for amplifying electret microphones in situations where the loudness of the audio isn't predictable. This fancy microphone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
  WS2812 RGB LED strip: WS2812 strip
  Trimpot-#3296-flat: Bourns #3296 Square Trimpot 25 turn lying flat for low profile
